# Fritzing sketch Arduino-Android-Telefon-ile-Bluetooth-Kontrollü-Araba (saved by Fritzing 0.9.3b)
breadboards: 1

parts:
  Parça1 = Arduino Uno (Rev3)
  VCC1 = Battery block 9V
  M1 = DC Motor
  M2 = DC Motor
  M3 = DC Motor
  M4 = DC Motor
  L298N1 = L298_BRIDGE_DRIVER [package=powerso20]
  LED1 = LED - 5mm [color="Red (633nm)" package="5 mm [THT]"]
  LED2 = LED - 5mm [color="Red (633nm)" package="5 mm [THT]"]
  J1 = Piezo Speaker
  R3 = Resistor [tolerance=±5% resistance=220 package=THT]
  R4 = Resistor [tolerance=±5% resistance=220 package=THT]

nets:
  5V: Parça1.5V, L298N1.VSS
  N1: VCC1.-, L298N1.GND, J1.pin1, R3.Pin_1, R4.Pin_1
  N2: VCC1.+, L298N1.VS
  N3: M1.pin_1, M2.pin_1, L298N1.OUT4
  N4: M1.pin_2, M2.pin_2, L298N1.OUT3
  N5: M3.pin_1, M4.pin_1, L298N1.OUT2
  N6: M3.pin_2, M4.pin_2, L298N1.OUT1
  N7: LED1.cathode, R3.Pin_0
  N8: LED2.cathode, R4.Pin_0
